// Logisim project control_logic.circ as structural Verilog: 1 circuit, main circuit control_logic
module control_logic (
  input  [31:0] inst,
  input  BrEq,
  input  BrLt,
  output PCSel,
  output RegWEn,
  output [2:0] ImmSel,
  output BrUn,
  output ASel,
  output BSel,
  output [3:0] ALUSel,
  output MemRW,
  output [1:0] WBSel,
  output CSRSel,
  output CSRWen
);

  wire ALU_and, ALU_BSel, ALU_mul, ALU_mulh, ALU_mulhu, ALU_or, ALU_plus, ALU_sll, ALU_slt, ALU_sra, ALU_srl,
       ALU_sub, ALU_xor, and_1_out, and_3_out, and_4_out, and_8_out, and_14_out, and_18_out, and_19_out,
       and_21_out, and_22_out, and_23_out, and_24_out, and_27_out, and_28_out, and_30_out, and_31_out, Comp,
       comparator_2_eq, comparator_3_eq, I, I_csrw, I_csrwi, I_imm, I_jalr, I_mem, not_1_out, not_2_out,
       or_7_out, or_8_out, or_10_out, or_11_out, R, R_sll, R_srl, RI_plus, RV32I, SB, U, U_auipc, UJ;

  and and_1 (and_1_out, RV32I, ~inst[2], ~inst[3], ~inst[5], ~inst[6]);  // AND_Gate
  and and_2 (I_jalr, RV32I, inst[2], ~inst[3], ~inst[4], inst[5], inst[6]);  // AND_Gate
  and and_3 (and_3_out, inst[12], ~inst[13], ~inst[14]);  // AND_Gate
  and and_4 (and_4_out, inst[12], ~inst[13], inst[14]);  // AND_Gate
  and and_5 (R, RV32I, ~inst[2], ~inst[3], inst[4], inst[5], ~inst[6]);  // AND_Gate
  and and_6 (I_mem, and_1_out, ~inst[4]);  // AND_Gate
  and and_7 (I_imm, and_1_out, inst[4]);
  and and_8 (and_8_out, RV32I, ~inst[2], ~inst[3], inst[4], inst[5], inst[6]);  // AND_Gate
  and and_9 (I_csrw, and_8_out, and_3_out);
  and and_10 (I_csrwi, and_8_out, and_4_out);
  or or_1 (I, I_mem, I_imm, I_jalr, I_csrw, I_csrwi);
  and and_11 (RV32I, inst[0], inst[1]);
  and and_12 (MemRW, RV32I, ~inst[2], ~inst[3], ~inst[4], inst[5], ~inst[6]);  // AND_Gate
  and and_13 (SB, RV32I, ~inst[2], ~inst[3], ~inst[4], inst[5], inst[6]);  // AND_Gate
  and and_14 (and_14_out, RV32I, inst[2], ~inst[3], inst[4], ~inst[6]);  // AND_Gate
  and and_15 (UJ, RV32I, inst[2], inst[3], ~inst[4], inst[5], inst[6]);  // AND_Gate
  and and_16 (U_auipc, and_14_out, ~inst[5]);  // AND_Gate
  and and_17 (ALU_BSel, and_14_out, inst[5]);
  or or_2 (U, U_auipc, ALU_BSel);
  not not_1 (not_1_out, BrEq);
  not not_2 (not_2_out, BrLt);
  and and_18 (and_18_out, SB, Comp);
  or or_3 (RegWEn, R, I, U, UJ);
  and and_19 (and_19_out, I, ~I_csrwi);  // AND_Gate
  or or_4 (PCSel, and_18_out, UJ, I_jalr);
  Priority_Encoder priority_encoder_1 (
    .in0(and_19_out), .in1(MemRW), .in2(SB), .in3(U), .in4(UJ), .in5(I_csrwi), .out(ImmSel), .en_in(1'b1));  // open: in6, in7, gs, en_out
  and and_20 (BrUn, inst[13], inst[14]);
  or or_5 (ASel, SB, U_auipc, UJ);
  or or_6 (BSel, I, MemRW, SB, U, UJ);
  or or_7 (or_7_out, R, I_imm, U);
  Priority_Encoder #(.select(2)) priority_encoder_2 (
    .in0(or_7_out), .in1(I_mem), .in2(or_8_out), .out(WBSel), .en_in(1'b1));  // open: in3, gs, en_out
  or or_8 (or_8_out, UJ, I_jalr);
  Comparator #(.width(3)) comparator_1 (.a(inst[14:12]), .b(3'b101), .eq(CSRSel));  // open: gt, lt
  or or_9 (CSRWen, I_csrw, I_csrwi);
  Multiplexer #(.enable("false"), .select(3)) multiplexer_1 (
    .in0(BrEq), .in1(not_1_out), .in4(BrLt), .in5(not_2_out), .in6(BrLt), .in7(not_2_out), .out(Comp),
    .sel(inst[14:12]));  // open: in2, in3
  and and_21 (and_21_out, ~inst[25], ~inst[30]);  // AND_Gate
  and and_22 (and_22_out, ~inst[25], ~inst[30]);  // AND_Gate
  and and_23 (and_23_out, ~inst[25], ~inst[30]);  // AND_Gate
  Priority_Encoder #(.select(4)) priority_encoder_3 (
    .in0(ALU_plus), .in1(ALU_and), .in2(ALU_or), .in3(ALU_xor), .in4(ALU_srl), .in5(ALU_sra), .in6(ALU_sll),
    .in7(ALU_slt), .in10(ALU_mul), .in11(ALU_mulhu), .in12(ALU_sub), .in13(ALU_BSel), .in14(ALU_mulh),
    .out(ALUSel), .en_in(1'b1));  // open: in8, in9, in15, gs, en_out
  and and_24 (and_24_out, R, and_21_out);
  and and_25 (ALU_srl, R_srl, and_22_out);
  and and_26 (ALU_sll, R_sll, and_23_out);
  or or_10 (or_10_out, and_24_out, I_imm);
  Demultiplexer #(.enable("false"), .select(3)) demultiplexer_1 (
    .out0(RI_plus), .out1(R_sll), .out2(ALU_slt), .out4(ALU_xor), .out5(R_srl), .out6(ALU_or),
    .out7(ALU_and), .in(or_10_out), .sel(inst[14:12]));  // open: out3
  or or_11 (or_11_out, R, I_imm);
  Comparator #(.width(3)) comparator_2 (.a(inst[14:12]), .b(3'b101), .eq(comparator_2_eq));  // open: gt, lt
  and and_27 (and_27_out, ~inst[25], inst[30]);  // AND_Gate
  and and_28 (and_28_out, inst[25], ~inst[30]);  // AND_Gate
  and and_29 (ALU_sra, or_11_out, comparator_2_eq, and_27_out);
  and and_30 (and_30_out, R, and_28_out);
  Comparator #(.width(3)) comparator_3 (.a(inst[14:12]), .b(3'b000), .eq(comparator_3_eq));  // open: gt, lt
  and and_31 (and_31_out, ~inst[25], inst[30]);  // AND_Gate
  or or_12 (ALU_plus, RI_plus, I_mem, MemRW, SB, U_auipc, UJ, I_jalr);
  Demultiplexer #(.enable("false"), .select(3)) demultiplexer_2 (
    .out0(ALU_mul), .out1(ALU_mulh), .out3(ALU_mulhu), .in(and_30_out), .sel(inst[14:12]));  // open: out2, out4, out5, out6, out7
  and and_32 (ALU_sub, R, comparator_3_eq, and_31_out);

  // Other names for the same wires on the sheet: opcode[6:0] = inst[6:0]; opc2 = inst[2]; opc3 = inst[3];
  //   opc4 = inst[4]; opc5 = inst[5]; opc6 = inst[6]; func3[2:0] = inst[14:12]; func3_0 = inst[12];
  //   func3_1 = inst[13]; func3_2 = inst[14]; func7_0 = inst[25]; func7_2[1:0] = {inst[30], inst[25]};
  //   func7_1 = inst[30]; S = MemRW; U_lui = ALU_BSel

  // Notes on the sheet:
  //   INPUTS to your circuit
  //   DON'T CHANGE THE LOCATIONS OF THE INPUTS AND OUTPUTS!
  //   OUTPUT from your circuit
endmodule
