// Logisim project branch_comp.circ as structural Verilog: 1 circuit, main circuit branch_comp
module branch_comp (
  input  [31:0] rs1,
  input  [31:0] rs2,
  input  BrUn,
  output BrEq,
  output BrLt
);

  wire BrEq_2C, BrEq_Un, BrLt_2C, BrLt_Un;

  Comparator #(.width(32)) comparator_1 (.a(rs1), .b(rs2), .eq(BrEq_2C), .lt(BrLt_2C));  // open: gt
  Comparator #(.mode("unsigned"), .width(32)) comparator_2 (.a(rs1), .b(rs2), .eq(BrEq_Un), .lt(BrLt_Un));  // open: gt
  Multiplexer #(.enable("false")) multiplexer_1 (.in0(BrEq_2C), .in1(BrEq_Un), .out(BrEq), .sel(BrUn));
  Multiplexer #(.enable("false")) multiplexer_2 (.in0(BrLt_2C), .in1(BrLt_Un), .out(BrLt), .sel(BrUn));

  // Notes on the sheet:
  //   INPUTS to your circuit
  //   DON'T CHANGE THE LOCATIONS OF THE INPUTS AND OUTPUTS!
  //   OUTPUT from your circuit
endmodule
