// Logisim project cpu.circ as structural Verilog: 1 circuit, main circuit cpu
module cpu (
  input  clk,
  input  [31:0] INSTRUCTION,
  input  [31:0] READ_DATA,
  output [31:0] WRITE_ADDRESS,
  output [31:0] PROGRAM_COUNTER,
  output [31:0] ra,
  output [31:0] sp,
  output [31:0] t0,
  output [31:0] t1,
  output [31:0] t2,
  output [31:0] s0,
  output [31:0] s1,
  output [31:0] a0,
  output [31:0] tohost,
  output [3:0] WRITE_ENABLE,
  output [31:0] WRITE_DATA
);

  wire ASel, BrEq, BrLt, BrUn, BSel, CSRSel, CSRWen, MemRW, PCSel, RegWEn;
  wire [1:0] WBSel;
  wire [2:0] func3, ImmSel;
  wire [3:0] ALUSel, bit_extender_1_out, multiplexer_6_out;
  wire [6:0] func7;
  wire [24:0] INSTRUCTION_PIPE;
  wire [31:0] adder_1_out, bit_extender_2_out, bit_extender_3_out, imm, multiplexer_1_out, multiplexer_2_out,
       multiplexer_3_out, outA, outB, PROGRAM_COUNTER_PIPE, read_data_1, READ_DATA_MASK, wb;

  Adder #(.width(32)) adder_1 (.a(PROGRAM_COUNTER), .b(32'h4), .out(adder_1_out));  // open: cin, cout
  Multiplexer #(.enable("false"), .width(32)) multiplexer_1 (
    .in0(adder_1_out), .in1(WRITE_ADDRESS), .out(multiplexer_1_out), .sel(PCSel));
  Register #(.width(32)) PC (.D(multiplexer_1_out), .en(1'b1), .clk(clk), .Q(PROGRAM_COUNTER));  // open: clr
  Multiplexer #(.enable("false"), .width(32)) multiplexer_2 (
    .in0(INSTRUCTION), .in1(32'h13), .out(multiplexer_2_out), .sel(PCSel));
  Register #(.width(32)) register_1 (
    .D(multiplexer_2_out), .en(1'b1), .clk(clk),
    .Q({func7, INSTRUCTION_PIPE[24:15], func3, INSTRUCTION_PIPE[11:0]}));  // open: clr
  Register #(.width(32)) register_2 (.D(PROGRAM_COUNTER), .en(1'b1), .clk(clk), .Q(PROGRAM_COUNTER_PIPE));  // open: clr
  regfile regfile_1 (
    .rs1(INSTRUCTION_PIPE[19:15]), .rs2(INSTRUCTION_PIPE[24:20]), .rd(INSTRUCTION_PIPE[11:7]),
    .Write_Data(wb), .RegWEn(RegWEn), .clk(clk), .ra(ra), .sp(sp), .t0(t0), .t1(t1), .t2(t2), .s0(s0),
    .s1(s1), .a0(a0), .Read_Data_1(read_data_1), .Read_Data_2(WRITE_DATA));
  branch_comp branch_comp_1 (.rs1(read_data_1), .rs2(WRITE_DATA), .BrUn(BrUn), .BrEq(BrEq), .BrLt(BrLt));
  imm_gen imm_gen_1 (
    .inst({func7, INSTRUCTION_PIPE[24:15], func3, INSTRUCTION_PIPE[11:0]}), .ImmSel(ImmSel), .imm(imm));
  control_logic control_logic_1 (
    .CSRWen(CSRWen), .PCSel(PCSel), .RegWEn(RegWEn), .ImmSel(ImmSel), .BrUn(BrUn), .ASel(ASel), .BSel(BSel),
    .ALUSel(ALUSel), .MemRW(MemRW), .WBSel(WBSel), .CSRSel(CSRSel),
    .inst({func7, INSTRUCTION_PIPE[24:15], func3, INSTRUCTION_PIPE[11:0]}), .BrEq(BrEq), .BrLt(BrLt));
  Multiplexer #(.enable("false"), .width(32)) multiplexer_3 (
    .in0(outA), .in1(outB), .out(multiplexer_3_out), .sel(CSRSel));
  Multiplexer #(.enable("false"), .width(32)) multiplexer_4 (
    .in0(read_data_1), .in1(PROGRAM_COUNTER_PIPE), .out(outA), .sel(ASel));
  Multiplexer #(.enable("false"), .width(32)) multiplexer_5 (.in0(WRITE_DATA), .in1(imm), .out(outB), .sel(BSel));
  csr csr_1 (.CSR_address(12'h51e), .CSR_din(multiplexer_3_out), .CSR_WE(CSRWen), .clk(clk), .tohost(tohost));
  alu alu_1 (.Result(WRITE_ADDRESS), .A(outA), .B(outB), .ALUSel(ALUSel));
  Multiplexer #(.enable("false"), .select(2), .width(4)) multiplexer_6 (
    .in0(4'b0001), .in1(4'b0011), .in2(4'b1111), .out(multiplexer_6_out), .sel(func3[1:0]));  // open: in3
  assign bit_extender_1_out = {{3{MemRW}}, MemRW};  // Bit_Extender bit_extender_1
  assign bit_extender_2_out = {{24{READ_DATA[7]}}, READ_DATA[7:0]};  // Bit_Extender bit_extender_2
  assign bit_extender_3_out = {{16{READ_DATA[15]}}, READ_DATA[15:0]};  // Bit_Extender bit_extender_3
  Multiplexer #(.enable("false"), .select(2), .width(32)) multiplexer_7 (
    .in0(WRITE_ADDRESS), .in1(READ_DATA_MASK), .in2(PROGRAM_COUNTER), .out(wb), .sel(WBSel));  // open: in3
  assign WRITE_ENABLE = multiplexer_6_out & bit_extender_1_out;  // AND_Gate and_1, 4 bits wide
  Multiplexer #(.enable("false"), .select(2), .width(32)) multiplexer_8 (
    .in0(bit_extender_2_out), .in1(bit_extender_3_out), .in2(READ_DATA), .out(READ_DATA_MASK),
    .sel(func3[1:0]));  // open: in3

  // Other names for the same wires on the sheet: ALUout[31:0] = WRITE_ADDRESS; opcode[6:0] = INSTRUCTION_PIPE[6:0];
  //   rd[4:0] = INSTRUCTION_PIPE[11:7]; INSTRUCTION_PIPE (some bits) = {func7, func3};
  //   rs1[4:0] = INSTRUCTION_PIPE[19:15]; rs2[4:0] = INSTRUCTION_PIPE[24:20]; read_data_2[31:0] = WRITE_DATA

  // Notes on the sheet:
  //   Output to IMEM
  //   IMEM (do **NOT** move this)
  //   Inputs from IMEM
  //   It is OK to move the PC, RegFile, ALU, MEM, Branch Comp, Imm Gen, and Control Logic to wherever is most convenient for you when constructing your CPU, and to delete this text
  //   Inputs/Outputs for testing. Do **NOT** move these.
  //   Outputs To DMEM
  //   DMEM (do **NOT** move this)
  //   Inputs From DMEM
endmodule
