// Logisim project regfile.circ as structural Verilog: 1 circuit, main circuit regfile
module regfile (
  input  [4:0] rs1,
  input  [4:0] rs2,
  input  [4:0] rd,
  input  [31:0] Write_Data,
  input  RegWEn,
  input  clk,
  output [31:0] ra,
  output [31:0] sp,
  output [31:0] t0,
  output [31:0] t1,
  output [31:0] t2,
  output [31:0] s0,
  output [31:0] s1,
  output [31:0] a0,
  output [31:0] Read_Data_1,
  output [31:0] Read_Data_2
);

  wire write1, write2, write3, write4, write5, write6, write7, write8, write9, write10, write11, write12,
       write13, write14, write15, write16, write17, write18, write19, write20, write21, write22, write23,
       write24, write25, write26, write27, write28, write29, write30, write31;
  wire [31:0] out3, out4, out11, out12, out13, out14, out15, out16, out17, out18, out19, out20, out21, out22,
       out23, out24, out25, out26, out27, out28, out29, out30, out31, x0;

  Register #(.width(32)) register_1 (.D(Write_Data), .en(1'b0), .clk(clk), .Q(x0));  // open: clr
  Register #(.width(32)) register_2 (.D(Write_Data), .en(write5), .clk(clk), .Q(t0));  // open: clr
  Register #(.width(32)) register_3 (.D(Write_Data), .en(write10), .clk(clk), .Q(a0));  // open: clr
  Register #(.width(32)) register_4 (.D(Write_Data), .en(write15), .clk(clk), .Q(out15));  // open: clr
  Register #(.width(32)) register_5 (.D(Write_Data), .en(write20), .clk(clk), .Q(out20));  // open: clr
  Register #(.width(32)) register_6 (.D(Write_Data), .en(write25), .clk(clk), .Q(out25));  // open: clr
  Register #(.width(32)) register_7 (.D(Write_Data), .en(write30), .clk(clk), .Q(out30));  // open: clr
  Register #(.width(32)) register_8 (.D(Write_Data), .en(write1), .clk(clk), .Q(ra));  // open: clr
  Register #(.width(32)) register_9 (.D(Write_Data), .en(write6), .clk(clk), .Q(t1));  // open: clr
  Register #(.width(32)) register_10 (.D(Write_Data), .en(write11), .clk(clk), .Q(out11));  // open: clr
  Register #(.width(32)) register_11 (.D(Write_Data), .en(write16), .clk(clk), .Q(out16));  // open: clr
  Register #(.width(32)) register_12 (.D(Write_Data), .en(write21), .clk(clk), .Q(out21));  // open: clr
  Register #(.width(32)) register_13 (.D(Write_Data), .en(write26), .clk(clk), .Q(out26));  // open: clr
  Register #(.width(32)) register_14 (.D(Write_Data), .en(write31), .clk(clk), .Q(out31));  // open: clr
  ROM rom_1 ();  // open: addr, data
  Register #(.width(32)) register_15 (.D(Write_Data), .en(write2), .clk(clk), .Q(sp));  // open: clr
  Register #(.width(32)) register_16 (.D(Write_Data), .en(write7), .clk(clk), .Q(t2));  // open: clr
  Register #(.width(32)) register_17 (.D(Write_Data), .en(write12), .clk(clk), .Q(out12));  // open: clr
  Register #(.width(32)) register_18 (.D(Write_Data), .en(write17), .clk(clk), .Q(out17));  // open: clr
  Register #(.width(32)) register_19 (.D(Write_Data), .en(write22), .clk(clk), .Q(out22));  // open: clr
  Register #(.width(32)) register_20 (.D(Write_Data), .en(write27), .clk(clk), .Q(out27));  // open: clr
  Register #(.width(32)) register_21 (.D(Write_Data), .en(write3), .clk(clk), .Q(out3));  // open: clr
  Register #(.width(32)) register_22 (.D(Write_Data), .en(write8), .clk(clk), .Q(s0));  // open: clr
  Register #(.width(32)) register_23 (.D(Write_Data), .en(write13), .clk(clk), .Q(out13));  // open: clr
  Register #(.width(32)) register_24 (.D(Write_Data), .en(write18), .clk(clk), .Q(out18));  // open: clr
  Register #(.width(32)) register_25 (.D(Write_Data), .en(write23), .clk(clk), .Q(out23));  // open: clr
  Register #(.width(32)) register_26 (.D(Write_Data), .en(write28), .clk(clk), .Q(out28));  // open: clr
  Register #(.width(32)) register_27 (.D(Write_Data), .en(write4), .clk(clk), .Q(out4));  // open: clr
  Register #(.width(32)) register_28 (.D(Write_Data), .en(write9), .clk(clk), .Q(s1));  // open: clr
  Register #(.width(32)) register_29 (.D(Write_Data), .en(write14), .clk(clk), .Q(out14));  // open: clr
  Register #(.width(32)) register_30 (.D(Write_Data), .en(write19), .clk(clk), .Q(out19));  // open: clr
  Register #(.width(32)) register_31 (.D(Write_Data), .en(write24), .clk(clk), .Q(out24));  // open: clr
  Register #(.width(32)) register_32 (.D(Write_Data), .en(write29), .clk(clk), .Q(out29));  // open: clr
  Multiplexer #(.enable("false"), .select(5), .width(32)) multiplexer_1 (
    .in0(x0), .in1(ra), .in2(sp), .in3(out3), .in4(out4), .in5(t0), .in6(t1), .in7(t2), .in8(s0), .in9(s1),
    .in10(a0), .in11(out11), .in12(out12), .in13(out13), .in14(out14), .in15(out15), .in16(out16),
    .in17(out17), .in18(out18), .in19(out19), .in20(out20), .in21(out21), .in22(out22), .in23(out23),
    .in24(out24), .in25(out25), .in26(out26), .in27(out27), .in28(out28), .in29(out29), .in30(out30),
    .in31(out31), .out(Read_Data_1), .sel(rs1));
  Multiplexer #(.enable("false"), .select(5), .width(32)) multiplexer_2 (
    .in0(x0), .in1(ra), .in2(sp), .in3(out3), .in4(out4), .in5(t0), .in6(t1), .in7(t2), .in8(s0), .in9(s1),
    .in10(a0), .in11(out11), .in12(out12), .in13(out13), .in14(out14), .in15(out15), .in16(out16),
    .in17(out17), .in18(out18), .in19(out19), .in20(out20), .in21(out21), .in22(out22), .in23(out23),
    .in24(out24), .in25(out25), .in26(out26), .in27(out27), .in28(out28), .in29(out29), .in30(out30),
    .in31(out31), .out(Read_Data_2), .sel(rs2));
  Demultiplexer #(.enable("false"), .select(5)) demultiplexer_1 (
    .out1(write1), .out2(write2), .out3(write3), .out4(write4), .out5(write5), .out6(write6), .out7(write7),
    .out8(write8), .out9(write9), .out10(write10), .out11(write11), .out12(write12), .out13(write13),
    .out14(write14), .out15(write15), .out16(write16), .out17(write17), .out18(write18), .out19(write19),
    .out20(write20), .out21(write21), .out22(write22), .out23(write23), .out24(write24), .out25(write25),
    .out26(write26), .out27(write27), .out28(write28), .out29(write29), .out30(write30), .out31(write31),
    .in(RegWEn), .sel(rd));  // open: out0

  // Other names for the same wires on the sheet: read_data1[31:0] = Read_Data_1; read_data2[31:0] = Read_Data_2;
  //   read_reg1[4:0] = rs1; read_reg2[4:0] = rs2; write_en = RegWEn; write_reg[4:0] = rd

  // Notes on the sheet:
  //   INPUTS to your circuit
  //   DON'T CHANGE THE LOCATIONS OF THE INPUTS AND OUTPUTS!
  //   These are DEBUG/TEST outputs from your circuit.
  //   OUTPUTS from your circuit
endmodule
