// Logisim project imm_gen.circ as structural Verilog: 1 circuit, main circuit imm_gen
module imm_gen (
  input  [31:0] inst,
  input  [2:0] ImmSel,
  output [31:0] imm
);

  wire [31:0] out_crswi, out_I;
  wire [31:5] out_S, out_SB;
  wire [31:20] out_UJ;

  assign out_I = {{20{inst[31]}}, inst[31:20]};  // Bit_Extender bit_extender_1
  assign out_S = {{20{inst[31]}}, inst[31:25]};  // Bit_Extender bit_extender_2
  assign {out_SB[31:12], out_SB[10:5]} = {{19{inst[31]}}, inst[31:25]};  // Bit_Extender bit_extender_3
  assign out_UJ = {{11{inst[31]}}, inst[31]};  // Bit_Extender bit_extender_4
  assign out_crswi = {{27{inst[19]}}, inst[19:15]};  // Bit_Extender bit_extender_5
  Multiplexer #(.enable("false"), .select(3), .width(32)) multiplexer_1 (
    .in0(out_I), .in1({out_S, inst[11:7]}), .in2({out_SB[31:12], inst[7], out_SB[10:5], inst[11:8], 1'b0}),
    .in3({inst[31:12], {12{1'b0}}}), .in4({out_UJ, inst[19:12], inst[20], inst[30:21], 1'b0}),
    .in5(out_crswi), .out(imm), .sel(ImmSel));  // open: in6, in7

  // Other names for the same wires on the sheet: out_S[4:0] = inst[11:7]; out_SB (some bits) = {inst[7], inst[11:8]};
  //   out_U[31:12] = inst[31:12]; out_UJ[19:1] = {inst[19:12], inst[20], inst[30:21]}

  // Notes on the sheet:
  //   INPUTS to your circuit
  //   DON'T CHANGE THE LOCATIONS OF THE INPUTS AND OUTPUTS!
  //   OUTPUT from your circuit
endmodule
